# Fritzing sketch wetterstation (saved by Fritzing 0.9.4)

parts:
  Bauteil1 = prefix0000_brezknfftq [part_number=OBO-T160-230]
  Temperatur/Luftfeuchtigkeit = BMP280
  R1 = Resistor [tolerance=±5% resistance=4.7k package=THT]  # not connected
  R2 = Resistor [tolerance=±5% resistance=4.7k package=THT]  # not connected
  U1 = ESP32-38PinWide [part_number=ESP32-38PinWide]  # not connected
  Helligkeitssensor = BH1750
  D1 = SOLAR-IXYS [package=solarbit-12x1]
  R3 = Resistor [tolerance=±5% resistance=220 package=THT]  # not connected
  S1 = Reed switch [package=THT]
  S2 = Reed switch [package=THT]
  R4 = Resistor [tolerance=±5% resistance=10k package=THT]  # not connected
  R5 = Resistor [tolerance=±5% resistance=10k package=THT]  # not connected
  Mikrofon = Breakout Board for Electret Microphone
  S3 = Reed switch [package=THT]
  S4 = Reed switch [package=THT]
  S5 = Reed switch [package=THT]
  S6 = Reed switch [package=THT]
  S7 = Reed switch [package=THT]
  S8 = Reed switch [package=THT]
  S9 = Reed switch [package=THT]
  S10 = Reed switch [package=THT]
  R6 = Resistor [tolerance=±5% resistance=1k package=THT]
  R7 = Resistor [tolerance=±5% resistance=8.2k package=THT]
  R8 = Resistor [tolerance=±5% resistance=2.2k package=THT]
  R9 = Resistor [tolerance=±5% resistance=3.9k package=THT]
  R10 = Resistor [tolerance=±5% resistance=16k package=THT]
  R11 = Resistor [tolerance=±5% resistance=33k package=THT]
  R12 = Resistor [tolerance=±5% resistance=64.9k package=THT]
  R13 = Resistor [tolerance=±5% resistance=120k package=THT]
  R14 = Resistor [tolerance=±5% resistance=10k package=THT]  # not connected

nets (from the breadboard view):
  N1: Bauteil1.J1004_1, Temperatur/Luftfeuchtigkeit.GND
  N2: Bauteil1.J1004_2, Temperatur/Luftfeuchtigkeit.SCL
  N3: Bauteil1.J1004_3, Temperatur/Luftfeuchtigkeit.SDA
  N4: Bauteil1.J1004_4, Temperatur/Luftfeuchtigkeit.VIN
  N5: Bauteil1.J1004_6, Mikrofon.AUD
  N6: Bauteil1.J1004_7, Mikrofon.GND
  N7: Bauteil1.J1004_8, Mikrofon.VCC
  N8: Bauteil1.J1005_1, Helligkeitssensor.GND, D1.C, S1.pin_1, S2.pin_1, R6.Pin_1, R7.Pin_1, R8.Pin_1, R9.Pin_1, R10.Pin_1, R11.Pin_1, R12.Pin_1, R13.Pin_1
  N9: Bauteil1.J1005_2, S2.pin_2
  N10: Bauteil1.J1005_3, S1.pin_2
  N11: Bauteil1.J1005_4, D1.A
  N12: Bauteil1.J1005_5, Helligkeitssensor.SDA, Helligkeitssensor.ADDR
  N13: Bauteil1.J1005_6, Helligkeitssensor.SCL
  N14: Bauteil1.J1005_7, Helligkeitssensor.VCC
  N15: Bauteil1.J1005_8, S3.pin_1, S4.pin_1, S5.pin_1, S6.pin_1, S7.pin_1, S8.pin_1, S9.pin_1, S10.pin_1
  N16: Bauteil1.P1015_0, Bauteil1.P1059_1
  N17: Bauteil1.P1020_0, Bauteil1.P1035_2
  N18: Bauteil1.P1020_2, Bauteil1.P1146_0
  N19: Bauteil1.P1024_0, Bauteil1.P1116_2
  N20: Bauteil1.P1024_1, Bauteil1.P1037_0
  N21: Bauteil1.P1025_2, Bauteil1.P1098_6
  N22: Bauteil1.P1030_1, Bauteil1.P1106_1
  N23: Bauteil1.P1030_2, Bauteil1.P1124_0
  N24: Bauteil1.P1035_0, Bauteil1.P1095_0
  N25: Bauteil1.P1040_2, Bauteil1.P1081_3
  N26: Bauteil1.P1047_0, Bauteil1.P1050_2
  N27: Bauteil1.P1054_0, Bauteil1.P1079_2
  N28: Bauteil1.P1054_1, Bauteil1.P1063_0
  N29: Bauteil1.P1055_2, Bauteil1.P1103_F
  N30: Bauteil1.P1059_0, Bauteil1.P1074_2
  N31: Bauteil1.P1060_2, Bauteil1.P1097_E
  N32: Bauteil1.P1069_2, Bauteil1.P1098_F
  N33: Bauteil1.P1078_2, Bauteil1.P1096_6
  N34: Bauteil1.P1081_0, Bauteil1.P1094_0
  N35: Bauteil1.P1081_9, Bauteil1.P1140_0
  N36: Bauteil1.P1081_F, Bauteil1.P1111_2
  N37: Bauteil1.P1082_B, Bauteil1.P1120_2
  N38: Bauteil1.P1088_A, Bauteil1.P1113_3
  N39: Bauteil1.P1088_B, Bauteil1.P1166_3
  N40: Bauteil1.P1088_C, Bauteil1.P1123_3
  N41: Bauteil1.P1088_D, Bauteil1.P1119_3
  N42: Bauteil1.P1090_2, Bauteil1.P1102_0
  N43: Bauteil1.P1102_1, Bauteil1.P1152_0
  N44: Bauteil1.P1124_2, Bauteil1.P1167_0
  N45: S3.pin_2, R13.Pin_0
  N46: S4.pin_2, R11.Pin_0
  N47: S5.pin_2, R9.Pin_0
  N48: S6.pin_2, R6.Pin_0
  N49: S7.pin_2, R7.Pin_0
  N50: S8.pin_2, R10.Pin_0
  N51: S9.pin_2, R8.Pin_0
  N52: S10.pin_2, R12.Pin_0

notes:
  Anemometer
  Regensensor
  Widerstandswerte für Windrichtungssensor

custom parts:
  BMP280: Temperature Humidity Barometric presure Sensor, I2C
  ESP32-38PinWide: Generic 38-Pin ESP32 with wide format (only access to one side of pins on a breadboard) based on Stephen Lilley's HiLetgo ESP-WROOM-32 ESP32 ESP-32S Development Board.
  BH1750: Light Sensor
